// Digital circuit HWK1_bitfulladder.dig as structural Verilog
module HWK1_bitfulladder (
  input  A,
  input  B,
  input  C_in,
  output SUM,
  output C_out
);

  wire and_1_out, and_2_out, or_1_out, xor_1_out;

  xor xor_1 (xor_1_out, A, B);
  and and_1 (and_1_out, A, B);
  or or_1 (or_1_out, A, B);
  xor xor_2 (SUM, xor_1_out, C_in);
  and and_2 (and_2_out, or_1_out, C_in);
  or or_2 (C_out, and_1_out, and_2_out);
endmodule
