// Digital circuit HWK1_2bitmltplier.dig as structural Verilog
module HWK1_2bitmltplier (
  input  A_1,
  input  A_0,
  input  B_1,
  input  B_0,
  output P_0,
  output P_3,
  output P_2,
  output P_1
);

  wire and_1_out, and_2_out, and_4_out, and_5_out, and_6_out;

  and and_1 (and_1_out, A_0, B_1);
  and and_2 (and_2_out, A_1, B_0);
  and and_3 (P_0, A_0, B_0);
  and and_4 (and_4_out, A_1, B_1);
  and and_5 (and_5_out, and_1_out, ~and_2_out);  // And
  and and_6 (and_6_out, and_2_out, ~and_1_out);  // And
  or or_1 (P_1, and_5_out, and_6_out);
  and and_7 (P_3, P_0, and_4_out);
  and and_8 (P_2, and_4_out, ~P_0);  // And
endmodule
