// Digital circuit HWK1_4bitrippleBlock.dig as structural Verilog
module HWK1_4bitrippleBlock (
  input  C_in,
  input  A_0,
  input  B_0,
  input  A_1,
  input  B_1,
  input  A_2,
  input  B_2,
  input  A_3,
  input  B_3,
  output S_0,
  output S_1,
  output S_2,
  output S_3,
  output C_out
);

  wire hwk1_bitfulladder_1_c_out, hwk1_bitfulladder_2_c_out, hwk1_bitfulladder_3_c_out;

  HWK1_bitfulladder hwk1_bitfulladder_1 (.A(A_0), .B(B_0), .C_in(C_in), .SUM(S_0), .C_out(hwk1_bitfulladder_1_c_out));
  HWK1_bitfulladder hwk1_bitfulladder_2 (
    .A(A_1), .B(B_1), .C_in(hwk1_bitfulladder_1_c_out), .SUM(S_1), .C_out(hwk1_bitfulladder_2_c_out));
  HWK1_bitfulladder hwk1_bitfulladder_3 (
    .A(A_2), .B(B_2), .C_in(hwk1_bitfulladder_2_c_out), .SUM(S_2), .C_out(hwk1_bitfulladder_3_c_out));
  HWK1_bitfulladder hwk1_bitfulladder_4 (.A(A_3), .B(B_3), .C_in(hwk1_bitfulladder_3_c_out), .SUM(S_3), .C_out(C_out));
endmodule
