// Digital circuit HWK1_4bitripplecircuit.dig as structural Verilog
module HWK1_4bitripplecircuit (
  input  A_0,
  input  B_0,
  input  A_1,
  input  B_1,
  input  A_2,
  input  B_2,
  input  A_3,
  input  B_3,
  input  in_9,
  output S_0,
  output C_out,
  output S_1,
  output S_2,
  output S_3
);

  wire and_1_out, and_2_out, and_3_out, and_4_out, and_5_out, and_6_out, and_7_out, and_8_out, or_1_out,
       or_2_out, or_3_out, xor_1_out, xor_2_out, xor_3_out, xor_4_out;

  xor xor_1 (xor_1_out, A_0, B_0);
  and and_1 (and_1_out, A_0, B_0);
  xor xor_2 (xor_2_out, A_1, B_1);
  and and_2 (and_2_out, A_1, B_1);
  xor xor_3 (xor_3_out, A_2, B_2);
  and and_3 (and_3_out, A_2, B_2);
  xor xor_4 (xor_4_out, A_3, B_3);
  and and_4 (and_4_out, A_3, B_3);
  xor xor_5 (S_0, xor_1_out, in_9);
  and and_5 (and_5_out, xor_1_out, in_9);
  xor xor_6 (S_1, xor_2_out, or_1_out);
  and and_6 (and_6_out, xor_2_out, or_1_out);
  xor xor_7 (S_2, or_2_out, xor_3_out);
  and and_7 (and_7_out, or_2_out, xor_3_out);
  xor xor_8 (S_3, or_3_out, xor_4_out);
  and and_8 (and_8_out, or_3_out, xor_4_out);
  or or_1 (or_1_out, and_5_out, and_1_out);
  or or_2 (or_2_out, and_6_out, and_2_out);
  or or_3 (or_3_out, and_7_out, and_3_out);
  or or_4 (C_out, and_8_out, and_4_out);
endmodule
